// Logisim project HEAP.circ as structural Verilog
module BOARD_BIG_ASM (
  input  START,
  output out_2
);

  wire button_1_out, CLK, CLR, d_ff_1_q, not_1_out, Write, Write_ASCII;
  wire [6:0] ASCII;
  wire [7:0] counter_1_q;
  wire [23:0] Dir_INPUT, Dir_MEMORY;
  wire [31:0] INPUT, MEMORY_IN, MEMORY_OUT;

  Button button_1 (.out(button_1_out));
  Clock clock_1 (.out(CLK));
  D_Flip_Flop d_ff_1 (.clk(CLK), .D(1'b1), .Q(d_ff_1_q), .reset(button_1_out));  // open: Qn, preset, en
  D_Flip_Flop d_ff_2 (.clk(CLK), .D(d_ff_1_q), .Qn(CLR), .reset(button_1_out));  // open: Q, preset, en
  BIG_ASM big_asm_1 (
    .DATA_INPUT(INPUT), .MEMORY_IN(MEMORY_OUT), .CLK(CLK), .CLR(CLR), .DIR_INPUT(Dir_INPUT),
    .MEMORY_OUT(MEMORY_IN), .DIR_MEMORY(Dir_MEMORY), .START(START), .Write_OUTPUT(Write), .ASCII(ASCII),
    .Write_ASCII(Write_ASCII), .END(out_2));
  MEMORY memory_1 (.DIR(Dir_MEMORY), .DATA_IN(MEMORY_IN), .WRITE(Write), .CLK(CLK), .CLR(CLR), .DATA_OUT(MEMORY_OUT));
  INPUT input_1 (.DIR(Dir_INPUT), .CLK(CLK), .DATA_OUT(INPUT));
  Counter counter_1 (.load(1'b0), .count(not_1_out), .Q(counter_1_q), .clk(CLK), .clr(CLR));  // open: D, carry
  not not_1 (not_1_out, out_2);
  // Probe on counter_1_q
  TTY #(.rows(32), .cols(60)) tty_1 (.data(ASCII), .clk(CLK), .we(Write_ASCII), .clr(CLR));

  // Other names for the same wires on the sheet: END = out_2

  // Notes on the sheet:
  //   COUNTER
  //   BOARD
endmodule

module INPUT (
  input  [23:0] DIR,
  input  CLK,
  output [31:0] DATA_OUT
);

  RAM #(.addrWidth(24), .dataWidth(32)) ram_1 (.addr(DIR), .data(DATA_OUT), .clk(CLK), .ld(1'b1));  // open: sel, clr
endmodule

module MEMORY (
  input  [23:0] DIR,
  input  [31:0] DATA_IN,
  input  WRITE,
  input  CLK,
  input  CLR,
  output [31:0] DATA_OUT
);

  wire not_1_out;

  // Probe on DIR
  not not_1 (not_1_out, WRITE);
  // Probe on DATA_IN
  RAM #(.addrWidth(24), .dataWidth(32), .bus("separate")) ram_1 (
    .addr(DIR), .din(DATA_IN), .data(DATA_OUT), .clk(CLK), .ld(not_1_out), .clr(CLR));  // open: str, sel
  // Probe on DATA_OUT
endmodule

module BIG_ASM (
  input  [31:0] DATA_INPUT,
  input  [31:0] MEMORY_IN,
  input  START,
  input  CLK,
  input  CLR,
  output [23:0] DIR_INPUT,
  output [31:0] MEMORY_OUT,
  output [23:0] DIR_MEMORY,
  output Write_OUTPUT,
  output END,
  output [6:0] ASCII,
  output Write_ASCII
);

  wire FINAL, LOAD, READY, READY_2, WRITE, WRITE_MEMORY, WRITE_OUTPUT_t;
  wire [23:0] A, DIR_MEMORY_LOAD, DIR_MEMORY_t, DIR_MEMORY_WRITE, I, J, N, Z;
  wire [31:0] MEMORY_IN_LOAD, MEMORY_IN_WRITE, MEMORY_OUT_t, MEMORY_OUT_WRITE, VECTOR_I, VECTOR_J, VECTOR_Z;

  WRITE_MEMORY write_memory_1 (
    .MEMORY_IN(MEMORY_IN_WRITE), .START(WRITE), .CLK(CLK), .CLR(CLR), .I(I), .A(A), .END(READY_2),
    .MEMORY_OUT(MEMORY_OUT_WRITE), .DIR_MEMORY(DIR_MEMORY_WRITE), .Write_OUTPUT(WRITE_OUTPUT_t));
  ARRAY_MEMORY array_memory_1 (
    .DATA_INPUT(DATA_INPUT), .MEMORY_IN(MEMORY_IN), .START(START), .CLK(CLK), .CLR(CLR),
    .DIR_INPUT(DIR_INPUT), .MEMORY_OUT(MEMORY_OUT_t), .DIR_MEMORY(DIR_MEMORY_t), .Write_OUTPUT(WRITE_MEMORY),
    .END(FINAL), .SIZE(N));
  MAIN main_1 (
    .CLK(CLK), .START(FINAL), .RST(CLR), .VECTOR_I(VECTOR_I), .VECTOR_J(VECTOR_J), .VECTOR_Z(VECTOR_Z),
    .I(I), .J(J), .WRITE(WRITE), .LOAD(LOAD), .Z(Z), .END(END), .N(N), .A(A), .READY_2(READY_2), .READY(READY));
  LOAD_MEMORY_2_0 load_memory_2_0_1 (
    .MEMORY_IN(MEMORY_IN_LOAD), .I(I), .J(J), .Z(Z), .CLK(CLK), .RST(CLR), .START(LOAD), .END(READY),
    .OUTPUT(DIR_MEMORY_LOAD), .VECTOR_I(VECTOR_I), .VECTOR_J(VECTOR_J), .VECTOR_Z(VECTOR_Z));

  assign Write_ASCII = 1'b1;

  // Other names for the same wires on the sheet: RST = CLR
endmodule

module PRINT_UDEC (
  input  [31:0] num,
  input  start,
  input  CLK,
  input  RST,
  output [6:0] ASCII,
  output Write_ASCII,
  output \end 
);

  wire _0_c, _0_n, demultiplexer_1_out0, demultiplexer_2_out0, demultiplexer_2_out1, demultiplexer_3_out0,
       demultiplexer_3_out1, IDLE_2_q, IDLE_3_q, IDLE_4_q, IDLE_q, Lc, Lc_0, Ln, Ln_0, or_1_out;
  wire [23:0] bit_extender_1_out;
  wire [31:0] c, c___1, c___1_t, divider_1_rem, memory_1_data_out, multiplexer_1_out, multiplexer_2_out,
       multiplexer_3_out, n, n___10, n___10___48;

  Multiplexer #(.width(32), .enable("false")) multiplexer_1 (
    .in0(num), .in1(n___10), .out(multiplexer_1_out), .sel(Lc_0));
  Divider #(.width(32)) divider_1 (.a(n), .b(32'ha), .out(n___10), .rem(divider_1_rem));  // open: upper
  Adder #(.width(32)) adder_1 (.a(divider_1_rem), .b(32'h30), .out(n___10___48));  // open: cin, cout
  or or_1 (or_1_out, demultiplexer_1_out0, \end );
  Register #(.width(32)) u_n (.D(multiplexer_1_out), .en(Ln), .Q(n), .clk(CLK), .clr(RST));
  D_Flip_Flop IDLE (.clk(CLK), .D(or_1_out), .Q(IDLE_q), .preset(RST));  // open: Qn, en, reset
  Demultiplexer #(.enable("false")) demultiplexer_1 (
    .out0(demultiplexer_1_out0), .out1(Ln_0), .in(IDLE_q), .sel(start));
  or or_2 (Write_ASCII, demultiplexer_3_out0, demultiplexer_2_out1);
  Multiplexer #(.width(32), .enable("false")) multiplexer_2 (
    .in0(c___1), .in1(c___1_t), .out(multiplexer_2_out), .sel(Write_ASCII));
  Adder #(.width(32)) adder_2 (.a(c), .b(32'h1), .out(c___1));  // open: cin, cout
  Subtractor #(.width(32)) subtractor_1 (.a(c), .b(32'h1), .out(c___1_t));  // open: bin, bout
  D_Flip_Flop IDLE_2 (.clk(CLK), .D(Ln_0), .Q(IDLE_2_q), .reset(RST));  // open: Qn, preset, en
  Register #(.width(32)) u_c (.D(multiplexer_2_out), .en(Lc), .Q(c), .clk(CLK), .clr(RST));
  or or_3 (Lc_0, IDLE_2_q, demultiplexer_3_out1);
  Multiplexer #(.width(32), .enable("false")) multiplexer_3 (
    .in0(c), .in1(c___1_t), .out(multiplexer_3_out), .sel(Write_ASCII));
  Comparator #(.width(32), .mode("unsigned")) comparator_1 (.a({32{1'b0}}), .b(n), .lt(_0_n));  // open: gt, eq
  Comparator #(.width(32), .mode("unsigned")) comparator_2 (.a({32{1'b0}}), .b(c), .lt(_0_c));  // open: gt, eq
  D_Flip_Flop IDLE_3 (.clk(CLK), .D(Write_ASCII), .Q(IDLE_3_q), .reset(RST));  // open: Qn, preset, en
  Demultiplexer #(.enable("false")) demultiplexer_2 (
    .out0(demultiplexer_2_out0), .out1(demultiplexer_2_out1), .in(IDLE_3_q), .sel(_0_c));
  Bit_Extender #(.in_width(32), .out_width(24)) bit_extender_1 (.in(multiplexer_3_out), .out(bit_extender_1_out));
  D_Flip_Flop IDLE_4 (.clk(CLK), .D(Lc_0), .Q(IDLE_4_q), .reset(RST));  // open: Qn, preset, en
  or or_4 (Lc, Lc_0, Write_ASCII);
  or or_5 (Ln, Ln_0, Lc_0);
  Demultiplexer #(.enable("false")) demultiplexer_3 (
    .out0(demultiplexer_3_out0), .out1(demultiplexer_3_out1), .in(IDLE_4_q), .sel(_0_n));
  D_Flip_Flop IDLE_5 (.clk(CLK), .D(demultiplexer_2_out0), .Q(\end ), .reset(RST));  // open: Qn, preset, en
  MEMORY memory_1 (
    .DIR(bit_extender_1_out), .DATA_IN(n___10___48), .WRITE(Lc_0), .CLK(CLK), .CLR(RST),
    .DATA_OUT(memory_1_data_out));
  Bit_Extender #(.in_width(32), .out_width(7)) bit_extender_2 (.in(memory_1_data_out), .out(ASCII));

  // Other names for the same wires on the sheet: Lc_1 = Write_ASCII; Sc = Write_ASCII; Ln_1 = Lc_0; Sn = Lc_0;
  //   Write = Lc_0
endmodule

module PRINT_DEC (
  input  [31:0] num,
  input  start,
  input  CLK,
  input  RST,
  output [6:0] ASCII,
  output Write_ASCII,
  output END
);

  wire demultiplexer_1_out0, demultiplexer_1_out1, demultiplexer_2_out0, demultiplexer_3_out0, end_t,
       IDLE_3_q, IDLE_q, or_1_out, or_2_out, or_3_out, S_ASCII, startUDEC, Write_ASCII_1;
  wire [6:0] ASCII_t;
  wire [31:0] multiplexer_1_out, negator_1_out;

  or or_1 (or_1_out, demultiplexer_1_out0, END);
  Negator #(.width(32)) negator_1 (.in(num), .out(negator_1_out));
  D_Flip_Flop IDLE (.clk(CLK), .D(or_1_out), .Q(IDLE_q), .preset(RST));  // open: Qn, en, reset
  Demultiplexer #(.enable("false")) demultiplexer_1 (
    .out0(demultiplexer_1_out0), .out1(demultiplexer_1_out1), .in(IDLE_q), .sel(start));
  Multiplexer #(.width(32), .enable("false")) multiplexer_1 (
    .in0(num), .in1(negator_1_out), .out(multiplexer_1_out), .sel(num[31]));
  Demultiplexer #(.enable("false")) demultiplexer_2 (
    .out0(demultiplexer_2_out0), .out1(S_ASCII), .in(demultiplexer_1_out1), .sel(num[31]));
  or or_2 (or_2_out, demultiplexer_2_out0, S_ASCII);
  D_Flip_Flop IDLE_2 (.clk(CLK), .D(or_2_out), .Q(startUDEC), .reset(RST));  // open: Qn, preset, en
  PRINT_UDEC print_udec_1 (
    .num(multiplexer_1_out), .start(startUDEC), .CLK(CLK), .RST(RST), .ASCII(ASCII_t),
    .Write_ASCII(Write_ASCII_1), .\end (end_t));
  D_Flip_Flop IDLE_3 (.clk(CLK), .D(or_3_out), .Q(IDLE_3_q), .reset(RST));  // open: Qn, preset, en
  or or_3 (or_3_out, startUDEC, demultiplexer_3_out0);
  Demultiplexer #(.enable("false")) demultiplexer_3 (
    .out0(demultiplexer_3_out0), .out1(END), .in(IDLE_3_q), .sel(end_t));
  Multiplexer #(.width(7), .enable("false")) multiplexer_2 (
    .in0(ASCII_t), .in1(7'b0101101), .out(ASCII), .sel(S_ASCII));
  or or_4 (Write_ASCII, S_ASCII, Write_ASCII_1);

  // Other names for the same wires on the sheet: sign = num[31]; Write_ASCII_0 = S_ASCII
endmodule

module TEST_PRINT (
  input  [31:0] in_1,
  output out_2
);

  wire button_1_out, button_2_out, CLK, CLR, d_ff_1_q, Write_ASCII;
  wire [6:0] ASCII;

  Button button_1 (.out(button_1_out));
  Clock clock_1 (.out(CLK));
  D_Flip_Flop d_ff_1 (.clk(CLK), .D(1'b1), .Q(d_ff_1_q), .reset(button_1_out));  // open: Qn, preset, en
  D_Flip_Flop d_ff_2 (.clk(CLK), .D(d_ff_1_q), .Qn(CLR), .reset(button_1_out));  // open: Q, preset, en
  Button button_2 (.out(button_2_out));
  PRINT_UDEC print_udec_1 ();  // open: num, start, CLK, RST, ASCII, Write_ASCII, end
  PRINT_DEC print_dec_1 (
    .num(in_1), .start(button_2_out), .CLK(CLK), .RST(CLR), .ASCII(ASCII), .Write_ASCII(Write_ASCII),
    .END(out_2));
  TTY #(.rows(32), .cols(60)) tty_1 (.data(ASCII), .clk(CLK), .we(Write_ASCII), .clr(CLR));
endmodule

module DATAPATH (
  input  [23:0] size,
  input  [31:0] VECTOR_I,
  input  [31:0] VECTOR_J,
  input  [31:0] VECTOR_Z,
  input  SI,
  input  LI,
  input  SJ,
  input  LJ,
  input  SZ,
  input  LZ,
  input  SA,
  input  LA,
  input  RST,
  input  CLK,
  output [23:0] I,
  output WHILE_CONDITION,
  output VECTOR_J____VECTOR_Z,
  output [23:0] J,
  output N__1,
  output [23:0] Z,
  output [23:0] A,
  output N__2I_1,
  output N__2I_2
);

  wire comparator_3_gt, comparator_4_gt;
  wire [23:0] _2I_1, _2I_2, multiplexer_1_out, multiplexer_2_out, multiplexer_3_out, multiplexer_4_out,
       multiplier_1_out;

  Multiplexer #(.width(24), .enable("false")) multiplexer_1 (
    .in0({24{1'b0}}), .in1(A), .out(multiplexer_1_out), .sel(SI));
  Multiplexer #(.width(24), .enable("false")) multiplexer_2 (.in0(I), .in1(_2I_1), .out(multiplexer_2_out), .sel(SJ));
  Multiplexer #(.width(24), .enable("false")) multiplexer_3 (.in0(J), .in1(_2I_2), .out(multiplexer_3_out), .sel(SZ));
  Multiplexer #(.width(24), .enable("false")) multiplexer_4 (.in0(Z), .in1(J), .out(multiplexer_4_out), .sel(SA));
  Register #(.width(24)) u_I (.D(multiplexer_1_out), .en(LI), .Q(I), .clk(CLK), .clr(RST));
  Register #(.width(24)) u_J (.D(multiplexer_2_out), .en(LJ), .Q(J), .clk(CLK), .clr(RST));
  Register #(.width(24)) u_Z (.D(multiplexer_3_out), .en(LZ), .Q(Z), .clk(CLK), .clr(RST));
  Register #(.width(24)) u_A (.D(multiplexer_4_out), .en(LA), .Q(A), .clk(CLK), .clr(RST));
  Multiplier #(.width(24)) multiplier_1 (.a(I), .b(24'h2), .out(multiplier_1_out));  // open: cin, cout
  Comparator #(.width(24), .mode("unsigned")) comparator_1 (.a(size), .b(_2I_1), .gt(N__2I_1));  // open: eq, lt
  Comparator #(.width(24), .mode("unsigned")) comparator_2 (.a(size), .b(_2I_2), .gt(N__2I_2));  // open: eq, lt
  Comparator #(.width(32), .mode("unsigned")) comparator_3 (
    .a(VECTOR_I), .b(VECTOR_J), .gt(comparator_3_gt));  // open: eq, lt
  Comparator #(.width(32), .mode("unsigned")) comparator_4 (
    .a(VECTOR_I), .b(VECTOR_Z), .gt(comparator_4_gt));  // open: eq, lt
  Comparator #(.width(32), .mode("unsigned")) comparator_5 (
    .a(VECTOR_J), .b(VECTOR_Z), .lt(VECTOR_J____VECTOR_Z));  // open: gt, eq
  Comparator #(.width(24), .mode("unsigned")) comparator_6 (.a(size), .b(24'h1), .eq(N__1));  // open: gt, lt
  Adder #(.width(24)) adder_1 (.a(multiplier_1_out), .b(24'h1), .out(_2I_1));  // open: cin, cout
  or or_1 (WHILE_CONDITION, comparator_3_gt, comparator_4_gt);
  Adder #(.width(24)) adder_2 (.a(_2I_1), .b(24'h1), .out(_2I_2));  // open: cin, cout

  // Other names for the same wires on the sheet: N[23:0] = size
endmodule

module CONTROL_UNIT (
  input  vector_j____vector_z,
  input  Start,
  input  N__1,
  input  N___2i_2,
  input  rst,
  input  N_2i_1,
  input  conditional,
  input  clk,
  input  READY,
  input  READY_2,
  output End,
  output LOAD,
  output SI,
  output LI,
  output SJ,
  output LJ,
  output SZ,
  output LZ,
  output SA,
  output LA,
  output WRITE
);

  wire CONTINUE_0, demultiplexer_1_out0, demultiplexer_1_out1, demultiplexer_2_out0, demultiplexer_2_out1,
       demultiplexer_3_out0, demultiplexer_5_out0, demultiplexer_7_out0, demultiplexer_8_out0, END_2, END_t,
       IDLE_2_q, IDLE_q, INSIDE, or_2_out, or_5_out, or_7_out;

  D_Flip_Flop IDLE (.clk(clk), .D(demultiplexer_1_out0), .Q(IDLE_q), .preset(rst));  // open: Qn, en, reset
  Demultiplexer #(.enable("false")) demultiplexer_1 (
    .out0(demultiplexer_1_out0), .out1(demultiplexer_1_out1), .in(IDLE_q), .sel(Start));
  D_Flip_Flop IDLE_2 (.clk(clk), .D(LI), .Q(IDLE_2_q), .reset(rst));  // open: Qn, preset, en
  or or_1 (LI, CONTINUE_0, SI);
  Demultiplexer #(.enable("false")) demultiplexer_2 (
    .out0(demultiplexer_2_out0), .out1(demultiplexer_2_out1), .in(or_2_out), .sel(READY));
  or or_2 (or_2_out, demultiplexer_2_out0, LOAD);
  Demultiplexer #(.enable("false")) demultiplexer_3 (
    .out0(demultiplexer_3_out0), .out1(SA), .in(INSIDE), .sel(vector_j____vector_z));
  Demultiplexer #(.enable("false")) demultiplexer_4 (
    .out0(CONTINUE_0), .out1(END_t), .in(demultiplexer_1_out1), .sel(N__1));
  Demultiplexer #(.enable("false")) demultiplexer_5 (
    .out0(demultiplexer_5_out0), .out1(SJ), .in(IDLE_2_q), .sel(N_2i_1));
  Demultiplexer #(.enable("false")) demultiplexer_6 (
    .out0(END_2), .out1(INSIDE), .in(demultiplexer_2_out1), .sel(conditional));
  or or_3 (LA, demultiplexer_3_out0, SA);
  or or_4 (LJ, demultiplexer_5_out0, SJ);
  or or_5 (or_5_out, demultiplexer_7_out0, LA);
  Demultiplexer #(.enable("false")) demultiplexer_7 (
    .out0(demultiplexer_7_out0), .out1(SI), .in(or_5_out), .sel(READY_2));
  Demultiplexer #(.enable("false")) demultiplexer_8 (.out0(demultiplexer_8_out0), .out1(SZ), .in(LJ), .sel(N___2i_2));
  or or_6 (LOAD, demultiplexer_8_out0, SZ);
  or or_7 (or_7_out, END_2, End, END_t);
  D_Flip_Flop u_END (.clk(clk), .D(or_7_out), .Q(End), .reset(rst));  // open: Qn, preset, en

  assign LZ = LOAD;
  assign WRITE = LA;

  // Other names for the same wires on the sheet: FINAL = End; LA0 = LA; LI0 = LI; LJ0 = LJ; N_2i_2 = N___2i_2;
  //   reset = rst; SA0 = SA; CONTINUE_1 = SI; SI0 = SI; SJ0 = SJ; SZ0 = SZ; LZ0 = LOAD; WHILE = LOAD
endmodule

module MAIN (
  input  CLK,
  input  START,
  input  RST,
  input  [23:0] N,
  input  [31:0] VECTOR_I,
  input  READY_2,
  input  READY,
  input  [31:0] VECTOR_J,
  input  [31:0] VECTOR_Z,
  output [23:0] I,
  output [23:0] J,
  output WRITE,
  output LOAD,
  output [23:0] Z,
  output END,
  output [23:0] A
);

  wire LA, LI, LJ, LZ, N__1, N___2i_1, N___2i_2, SA, SI, SJ, SZ, VECTOR_J____VECTOR_Z, WHILE;

  // DATAPATH datapath_1: pin names not known; wires that end beside it: N, VECTOR_I, VECTOR_J, VECTOR_Z, SI, LI, SJ, LJ, SZ, LZ, SA, LA, RST, CLK, WHILE, I, VECTOR_J____VECTOR_Z, J, N__1, Z, A, N___2i_1, N___2i_2
  CONTROL_UNIT control_unit_1 (
    .vector_j____vector_z(VECTOR_J____VECTOR_Z), .Start(START), .N__1(N__1), .N___2i_2(N___2i_2), .rst(RST),
    .N_2i_1(N___2i_1), .conditional(WHILE), .clk(CLK), .End(END), .LOAD(LOAD), .SI(SI), .LI(LI), .SJ(SJ),
    .LJ(LJ), .SZ(SZ), .LZ(LZ), .SA(SA), .LA(LA), .WRITE(WRITE), .READY(READY), .READY_2(READY_2));
endmodule

module WRITE_MEMORY (
  input  [31:0] MEMORY_IN,
  input  START,
  input  CLK,
  input  CLR,
  input  [23:0] I,
  input  [23:0] A,
  output END,
  output [31:0] MEMORY_OUT,
  output [23:0] DIR_MEMORY,
  output Write_OUTPUT
);

  wire CHANGE, CHANGE_1, CHANGE_2, demultiplexer_1_out0, demultiplexer_1_out1, IDLE_5_q, IDLE_q, LA, or_1_out;
  wire [31:0] VALUE_IN_A, VALUE_IN_I;

  or or_1 (or_1_out, CLR, END);
  D_Flip_Flop IDLE (.clk(CLK), .D(demultiplexer_1_out0), .Q(IDLE_q), .preset(or_1_out));  // open: Qn, en, reset
  Demultiplexer #(.enable("false")) demultiplexer_1 (
    .out0(demultiplexer_1_out0), .out1(demultiplexer_1_out1), .in(IDLE_q), .sel(START));
  Register #(.width(32)) register_1 (.D(MEMORY_IN), .en(CHANGE_1), .Q(VALUE_IN_I), .clk(CLK), .clr(CLR));
  Register #(.width(32)) register_2 (.D(MEMORY_IN), .en(LA), .Q(VALUE_IN_A), .clk(CLK), .clr(CLR));
  D_Flip_Flop IDLE_2 (.clk(CLK), .D(demultiplexer_1_out1), .Q(CHANGE_1), .reset(CLR));  // open: Qn, preset, en
  D_Flip_Flop IDLE_3 (.clk(CLK), .D(CHANGE_1), .Q(LA), .reset(CLR));  // open: Qn, preset, en
  D_Flip_Flop IDLE_4 (.clk(CLK), .D(LA), .Q(CHANGE_2), .reset(CLR));  // open: Qn, preset, en
  or or_2 (CHANGE, CHANGE_1, CHANGE_2);
  D_Flip_Flop IDLE_5 (.D(CHANGE_2), .Q(IDLE_5_q), .reset(CLR));  // open: clk, Qn, preset, en
  D_Flip_Flop u_END (.clk(CLK), .D(IDLE_5_q), .Q(END), .reset(CLR));  // open: Qn, preset, en
  Multiplexer #(.width(32), .enable("false")) multiplexer_1 (
    .in0(VALUE_IN_I), .in1(VALUE_IN_A), .out(MEMORY_OUT), .sel(LA));
  // Probe on A
  // Probe on I
  Multiplexer #(.width(24), .enable("false")) multiplexer_2 (.in0(I), .in1(A), .out(DIR_MEMORY), .sel(CHANGE));
  or or_3 (Write_OUTPUT, LA, CHANGE_2);

  // Other names for the same wires on the sheet: LI = CHANGE_1; RST = CLR; WRITE = START; SELEC = LA;
  //   WRITE_IN_OUTPUT_0 = LA; WRITE_IN_OUTPUT_1 = CHANGE_2
endmodule

module ARRAY_MEMORY (
  input  [31:0] DATA_INPUT,
  input  [31:0] MEMORY_IN,
  input  START,
  input  CLK,
  input  CLR,
  output [23:0] DIR_INPUT,
  output [31:0] MEMORY_OUT,
  output [23:0] DIR_MEMORY,
  output Write_OUTPUT,
  output [23:0] SIZE,
  output END
);

  wire comparator_1_eq, comparator_1_gt, conditional, demultiplexer_1_out0, demultiplexer_2_out0,
       demultiplexer_3_out0, I__1, I_N_1, IDLE_2_q, IDLE_q, LAST, LI, LN, LOAD, LOAD1, or_5_out, SI,
       WHILE_2_q, WHILE_3_q;
  wire [1:1] N_1;
  wire [23:0] I, I_1, multiplexer_1_out, multiplexer_2_out, N, undriven;
  wire [31:0] AUX, multiplexer_4_out, subtractor_2_out, undriven_2;

  D_Flip_Flop IDLE (.clk(CLK), .D(demultiplexer_1_out0), .Q(IDLE_q), .preset(CLR));  // open: Qn, en, reset
  Multiplexer #(.width(24), .enable("false")) multiplexer_1 (.in0(24'h1), .in1(I_1), .out(multiplexer_1_out), .sel(SI));
  Demultiplexer #(.enable("false")) demultiplexer_1 (.out0(demultiplexer_1_out0), .out1(LN), .in(IDLE_q), .sel(START));
  Demultiplexer #(.enable("false")) demultiplexer_2 (
    .out0(demultiplexer_2_out0), .out1(LAST), .in(conditional), .sel(I__1));
  Register #(.width(24)) u_I (.D(multiplexer_1_out), .en(LI), .Q(I), .clk(CLK), .clr(CLR));
  // Probe on DATA_INPUT
  D_Flip_Flop IDLE_2 (.clk(CLK), .D(LN), .Q(IDLE_2_q), .reset(CLR));  // open: Qn, preset, en
  Register #(.width(32)) u_AUX (.D(DATA_INPUT), .en(LAST), .Q(AUX), .clk(CLK), .clr(CLR));
  Subtractor #(.width(24)) subtractor_1 (.a(N), .b(24'h1), .out(SIZE));  // open: bin, bout
  D_Flip_Flop WHILE (.clk(CLK), .D(LAST), .Q(N_1[1]), .reset(CLR));  // open: Qn, preset, en
  or or_1 (LI, SI, IDLE_2_q);
  Register #(.width(24)) u_N (.D(DATA_INPUT[23:0]), .en(LN), .Q(N), .clk(CLK), .clr(CLR));
  Comparator #(.width(24), .mode("unsigned")) comparator_1 (
    .a(SIZE), .b(I), .gt(comparator_1_gt), .eq(comparator_1_eq));  // open: lt
  D_Flip_Flop WHILE_2 (.clk(CLK), .D(LI), .Q(WHILE_2_q), .reset(CLR));  // open: Qn, preset, en
  Subtractor #(.width(32)) subtractor_2 (.a(DATA_INPUT), .b(32'h1), .out(subtractor_2_out));  // open: bin, bout
  Multiplexer #(.select(2), .width(24), .enable("false")) multiplexer_2 (
    .in0(I), .in1({24{1'b0}}), .in2(24'h1), .in3(undriven), .out(multiplexer_2_out), .sel({N_1[1], LN}));
  or or_2 (I_N_1, comparator_1_gt, comparator_1_eq);
  Demultiplexer #(.enable("false")) demultiplexer_3 (
    .out0(demultiplexer_3_out0), .out1(conditional), .in(WHILE_2_q), .sel(I_N_1));
  or or_3 (LOAD1, demultiplexer_2_out0, N_1[1]);
  Multiplexer #(.width(24), .enable("false")) multiplexer_3 (.in0(I), .in1(N), .out(DIR_INPUT), .sel(LAST));
  Multiplexer #(.select(2), .width(32), .enable("false")) multiplexer_4 (
    .in0(DATA_INPUT), .in1(subtractor_2_out), .in2(AUX), .in3(undriven_2), .out(multiplexer_4_out),
    .sel({N_1[1], LN}));
  Comparator #(.width(24), .mode("unsigned")) comparator_2 (.a(I), .b(24'h1), .eq(I__1));  // open: gt, lt
  Adder #(.width(24)) adder_1 (.a(I), .b(24'h1), .out(I_1));  // open: cin, cout
  Register #(.width(32)) MEMORY (.D(multiplexer_4_out), .en(LOAD), .Q(MEMORY_OUT), .clk(CLK), .clr(CLR));
  Register #(.width(24)) DIR (.D(multiplexer_2_out), .en(LOAD), .Q(DIR_MEMORY), .clk(CLK), .clr(CLR));
  D_Flip_Flop WHILE_3 (.clk(CLK), .D(LOAD1), .Q(WHILE_3_q), .reset(CLR));  // open: Qn, preset, en
  D_Flip_Flop WHILE_4 (.clk(CLK), .D(WHILE_3_q), .Q(SI), .reset(CLR));  // open: Qn, preset, en
  or or_4 (LOAD, LOAD1, LN);
  // Probe on {N_1[1], LN}
  or or_5 (or_5_out, END, demultiplexer_3_out0);
  or or_6 (Write_OUTPUT, LN, LOAD1);
  D_Flip_Flop u_END (.clk(CLK), .D(or_5_out), .Q(END), .reset(CLR));  // open: Qn, preset, en

  // Other names for the same wires on the sheet: LAUX = LAST; LOAD0 = LN; N_1[0] = LN; N_1_0 = LN; WRITE0 = LN;
  //   N_1_1 = N_1[1]; RST = CLR; WRITE1 = LOAD1
endmodule

module LOAD_MEMORY_2_0 (
  input  [31:0] MEMORY_IN,
  input  [23:0] I,
  input  [23:0] J,
  input  [23:0] Z,
  input  CLK,
  input  RST,
  input  START,
  output END,
  output [23:0] OUTPUT,
  output [31:0] VECTOR_I,
  output [31:0] VECTOR_Z,
  output [31:0] VECTOR_J
);

  wire Clk_t, demultiplexer_1_out0, IDLE_q, LI, LJ, LZ, reset, SI;
  wire [1:0] SELEC;

  D_Flip_Flop IDLE (.clk(CLK), .D(demultiplexer_1_out0), .Q(IDLE_q), .preset(RST));  // open: Qn, en, reset
  Demultiplexer #(.enable("false")) demultiplexer_1 (.out0(demultiplexer_1_out0), .out1(SI), .in(IDLE_q), .sel(START));
  or or_1 (SELEC[0], SI, LJ);
  or or_2 (SELEC[1], LI, LJ);
  Register #(.width(32)) u_I (.D(MEMORY_IN), .en(LI), .Q(VECTOR_I), .clk(CLK), .clr(RST));
  Register #(.width(32)) u_J (.D(MEMORY_IN), .en(LJ), .Q(VECTOR_J), .clk(CLK), .clr(RST));
  D_Flip_Flop IDLE_2 (.clk(CLK), .D(SI), .Q(LI));  // open: Qn, preset, en, reset
  D_Flip_Flop IDLE_3 (.clk(CLK), .D(LI), .Q(LJ));  // open: Qn, preset, en, reset
  Multiplexer #(.select(2), .width(24), .enable("false")) multiplexer_1 (
    .in0({24{1'b0}}), .in1(I), .in2(J), .in3(Z), .out(OUTPUT), .sel(SELEC));
  D_Flip_Flop IDLE_4 (.clk(CLK), .D(LJ), .Q(LZ));  // open: Qn, preset, en, reset
  Register #(.width(32)) u_Z (.D(MEMORY_IN), .en(LZ), .Q(VECTOR_Z), .clk(CLK), .clr(RST));
  D_Flip_Flop u_END (.clk(Clk_t), .D(LZ), .Q(END), .reset(reset));  // open: Qn, preset, en

  // Other names for the same wires on the sheet: SJ = LI; SZ = LJ
endmodule
